// Logisim project ex68.circ as structural Verilog: 1 circuit, main circuit main
module main (
  input  i2,
  input  i1,
  input  i0,
  output out_4,
  output out_5,
  output out_6,
  output out_7,
  output out_8,
  output out_9,
  output out_10,
  output out_11
);

  wire not_1_out, not_2_out, not_3_out;

  not not_1 (not_1_out, i2);
  not not_2 (not_2_out, i1);
  not not_3 (not_3_out, i0);
  and and_1 (out_4, not_1_out, not_2_out, not_3_out);
  and and_2 (out_5, i0, not_2_out, not_1_out);
  and and_3 (out_6, not_3_out, i1, not_1_out);
  and and_4 (out_7, i0, i1, not_1_out);
  and and_5 (out_8, not_3_out, not_2_out, i2);
  and and_6 (out_9, i0, not_2_out, i2);
  and and_7 (out_10, not_3_out, i1, i2);
  and and_8 (out_11, i0, i1, i2);
endmodule
