// Logisim project ex78.circ as structural Verilog: 1 circuit, main circuit main
module main (
  input  i2,
  input  i1,
  input  i0,
  input  i0_2,
  output out_5,
  output out_6,
  output out_7,
  output out_8,
  output out_9,
  output out_10,
  output out_11,
  output out_12
);

  wire not_1_out, not_2_out, not_3_out;

  not not_1 (not_1_out, i2);
  not not_2 (not_2_out, i1);
  not not_3 (not_3_out, i0);
  and and_1 (out_5, not_1_out, i0_2, not_2_out, not_3_out);
  and and_2 (out_6, i0, i0_2, not_2_out, not_1_out);
  and and_3 (out_7, not_3_out, i0_2, i1, not_1_out);
  and and_4 (out_8, i0, i0_2, i1, not_1_out);
  and and_5 (out_9, not_3_out, i0_2, not_2_out, i2);
  and and_6 (out_10, i0, i0_2, not_2_out, i2);
  and and_7 (out_11, not_3_out, i0_2, i1, i2);
  and and_8 (out_12, i0, i0_2, i1, i2);
endmodule
