// Logisim project ex4-14.circ as structural Verilog: 2 circuits, main circuit main
module main (
  input  [7:0] T,
  input  a,
  input  b,
  input  c,
  output [7:0] out_5
);

  _8bits_adder u_8bits_adder_1 (.a(T), .b({{5{1'b0}}, c, b, a}), .out_3(out_5));
endmodule

module _8bits_adder (
  input  [7:0] a,
  input  [7:0] b,
  output [7:0] out_3
);

  wire half_adder_1_cout, half_adder_2_cout, half_adder_3_cout, half_adder_4_cout, half_adder_5_cout,
       half_adder_6_cout, half_adder_7_cout;

  half_adder half_adder_1 (.cin(half_adder_2_cout), .a(a[1]), .b(b[1]), .out(out_3[1]), .cout(half_adder_1_cout));
  half_adder half_adder_2 (.cin(1'b0), .a(a[0]), .b(b[0]), .out(out_3[0]), .cout(half_adder_2_cout));
  half_adder half_adder_3 (.cin(half_adder_1_cout), .a(a[2]), .b(b[2]), .out(out_3[2]), .cout(half_adder_3_cout));
  half_adder half_adder_4 (.cin(half_adder_3_cout), .a(a[3]), .b(b[3]), .out(out_3[3]), .cout(half_adder_4_cout));
  half_adder half_adder_5 (.cin(half_adder_4_cout), .a(a[4]), .b(b[4]), .out(out_3[4]), .cout(half_adder_5_cout));
  half_adder half_adder_6 (.cin(half_adder_5_cout), .a(a[5]), .b(b[5]), .out(out_3[5]), .cout(half_adder_6_cout));
  half_adder half_adder_7 (.cin(half_adder_6_cout), .a(a[6]), .b(b[6]), .out(out_3[6]), .cout(half_adder_7_cout));
  half_adder half_adder_8 (.cin(half_adder_7_cout), .a(a[7]), .b(b[7]), .out(out_3[7]));  // open: cout
endmodule
