// Logisim project ex4-3.circ as structural Verilog
module main (
  input  [3:0] I,
  input  s0,
  input  s1,
  output [3:0] out_4,
  output [3:0] out_5
);

  wire clock_1_out;
  wire [3:0] n4bit4x1mux_1_out_7;

  _4bit4x1mux u_4bit4x1mux_1 (
    .in_1(out_4), .in_2(I), .in_3(4'b0000), .in_4(out_5), .out_7(n4bit4x1mux_1_out_7), .in_5(s0), .in_6(s1));
  Clock clock_1 (.out(clock_1_out));
  pure_4bit_reg pure_4bit_reg_1 (.out_3(out_4), .in_1(clock_1_out), .in_2(n4bit4x1mux_1_out_7));
  _4bitadder u_4bitadder_1 (.in_1(1'b1), .a(out_4), .a_2(4'b0000), .out_5(out_5));  // open: out_4

  // Other names for the same wires on the sheet: sum1[3:0] = out_5
endmodule

module _4bit4x1mux (
  input  [3:0] in_1,
  input  [3:0] in_2,
  input  [3:0] in_3,
  input  [3:0] in_4,
  input  in_5,
  input  in_6,
  output [3:0] out_7
);

  wire [3:0] and_1_out, and_2_out, and_3_out, and_4_out, and_5_out, and_6_out, and_7_out, and_8_out,
       not_1_out, not_2_out, not_3_out, not_4_out;

  assign not_1_out = ~{4{in_5}};  // NOT_Gate not_1, 4 bits wide
  assign not_2_out = ~{4{in_6}};  // NOT_Gate not_2, 4 bits wide
  assign not_3_out = ~{4{in_6}};  // NOT_Gate not_3, 4 bits wide
  assign not_4_out = ~{4{in_5}};  // NOT_Gate not_4, 4 bits wide
  assign and_1_out = in_1 & and_2_out;  // AND_Gate and_1, 4 bits wide
  assign and_2_out = not_1_out & not_2_out;  // AND_Gate and_2, 4 bits wide
  assign and_3_out = in_2 & and_4_out;  // AND_Gate and_3, 4 bits wide
  assign and_4_out = {4{in_5}} & not_3_out;  // AND_Gate and_4, 4 bits wide
  assign and_5_out = in_3 & and_6_out;  // AND_Gate and_5, 4 bits wide
  assign and_6_out = not_4_out & {4{in_6}};  // AND_Gate and_6, 4 bits wide
  assign and_7_out = in_4 & and_8_out;  // AND_Gate and_7, 4 bits wide
  assign and_8_out = {4{in_5}} & {4{in_6}};  // AND_Gate and_8, 4 bits wide
  assign out_7 = and_1_out | and_3_out | and_5_out | and_7_out;  // OR_Gate or_1, 4 bits wide

  // Other names for the same wires on the sheet: s0[3:0] = {4{in_5}}; s1[3:0] = {4{in_6}}
endmodule

module pure_4bit_reg (
  input  in_1,
  input  [3:0] in_2,
  output [3:0] out_3
);

  D_Flip_Flop d_ff_1 (.clk(in_1), .D(in_2[3]), .Q(out_3[3]));  // open: Qn, preset, en, reset
  D_Flip_Flop d_ff_2 (.clk(in_1), .D(in_2[2]), .Q(out_3[2]));  // open: Qn, preset, en, reset
  D_Flip_Flop d_ff_3 (.clk(in_1), .D(in_2[1]), .Q(out_3[1]));  // open: Qn, preset, en, reset
  D_Flip_Flop d_ff_4 (.clk(in_1), .D(in_2[0]), .Q(out_3[0]));  // open: Qn, preset, en, reset
endmodule

module half_adder (
  input  cin,
  input  a,
  input  b,
  output out,
  output cout
);

  wire and_1_out, and_2_out, xor_1_out;

  xor xor_1 (xor_1_out, a, b);
  xor xor_2 (out, cin, xor_1_out);
  and and_1 (and_1_out, xor_1_out, cin);
  and and_2 (and_2_out, a, b);
  xor xor_3 (cout, and_1_out, and_2_out);
endmodule

module _4bitadder (
  input  in_1,
  input  [3:0] a,
  input  [3:0] a_2,
  output out_4,
  output [3:0] out_5
);

  wire half_adder_1_cout, half_adder_2_cout, half_adder_3_cout;

  half_adder half_adder_1 (.cin(in_1), .a(a_2[0]), .b(a[0]), .out(out_5[0]), .cout(half_adder_1_cout));
  half_adder half_adder_2 (.cin(half_adder_1_cout), .a(a[1]), .b(a_2[1]), .out(out_5[1]), .cout(half_adder_2_cout));
  half_adder half_adder_3 (.cin(half_adder_2_cout), .a(a[2]), .b(a_2[2]), .out(out_5[2]), .cout(half_adder_3_cout));
  half_adder half_adder_4 (.cin(half_adder_3_cout), .a(a[3]), .b(a_2[3]), .out(out_5[3]), .cout(out_4));
endmodule
