// Logisim project prob1a.circ as structural Verilog: 1 circuit, main circuit main
module main (
  input  a,
  input  b,
  input  c,
  input  c_2,
  input  b_2,
  input  a_2,
  output F,
  output G
);

  wire and_1_out, and_2_out, and_3_out, and_4_out, and_5_out, not_1_out, not_2_out;

  and and_1 (and_1_out, a, b, c);
  not not_1 (not_1_out, b_2);
  and and_2 (and_2_out, a, b);
  not not_2 (not_2_out, a_2);
  or or_1 (F, a, and_2_out, c, and_1_out, b);
  and and_3 (and_3_out, c_2, not_1_out, a_2);
  and and_4 (and_4_out, c_2, not_1_out, not_2_out);
  and and_5 (and_5_out, a_2, b_2, c_2);
  or or_2 (G, and_3_out, and_4_out, and_5_out);
endmodule
