// Logisim project prob2.circ as structural Verilog: 1 circuit, main circuit main
module main (
  input  ER,
  input  DSBF,
  input  DOS,
  input  DC,
  input  DLC,
  input  KIC,
  input  DOS_2,
  input  BP,
  input  CM,
  output BELL,
  output DLA,
  output BA
);

  wire and_2_out, not_1_out, not_2_out, not_3_out, or_1_out, or_2_out;

  not not_1 (not_1_out, DSBF);
  not not_2 (not_2_out, DC);
  not not_3 (not_3_out, KIC);
  and and_1 (BA, BP, CM);
  and and_2 (and_2_out, not_1_out, DOS);
  or or_1 (or_1_out, not_3_out, DOS_2);
  and and_3 (DLA, DLC, or_1_out);
  or or_2 (or_2_out, and_2_out, not_2_out);
  and and_4 (BELL, ER, or_2_out);
endmodule
