// Logisim project prob6.circ as structural Verilog: 3 circuits, main circuit main
module main (
  input  C1,
  input  in_2,
  input  in_3,
  input  in_4,
  input  in_5,
  input  C6
);

  wire a, b, c, d, D1, D2, D3, D4, D5, D6, e, f, g, n6x3encoder_1_out_7, n6x3encoder_1_out_8,
       n6x3encoder_1_out_9;

  or or_1 (a, D3, D2, D5, D6);
  or or_2 (c, D1, D3, D4, D5, D6);
  or or_3 (b, D1, D2, D3, D4);
  or or_4 (d, D2, D3, D5, D6);
  _6x3Encoder u_6x3encoder_1 (
    .i0(C1), .in_2(in_2), .in_3(in_3), .in_4(in_4), .in_5(in_5), .i5(C6), .out_7(n6x3encoder_1_out_7),
    .out_8(n6x3encoder_1_out_8), .out_9(n6x3encoder_1_out_9));
  or or_5 (e, D2, D6);
  or or_6 (f, D4, D5, D6);
  or or_7 (g, D2, D3, D4, D5, D6);
  _3x6Decoder u_3x6decoder_1 (
    .i2(n6x3encoder_1_out_9), .i1(n6x3encoder_1_out_8), .i0(n6x3encoder_1_out_7), .out_5(D1), .out_6(D2),
    .out_7(D3), .out_8(D4), .out_9(D5), .out_10(D6));  // open: out_4, out_11
  _7_Segment_Display u_7_segment_display_1 (.g(g), .f(f), .a(a), .b(b), .e(e), .d(d), .c(c));  // open: dp
endmodule

module _3x6Decoder (
  input  i2,
  input  i1,
  input  i0,
  output out_4,
  output out_5,
  output out_6,
  output out_7,
  output out_8,
  output out_9,
  output out_10,
  output out_11
);

  wire not_1_out, not_2_out, not_3_out;

  not not_1 (not_1_out, i2);
  not not_2 (not_2_out, i1);
  not not_3 (not_3_out, i0);
  and and_1 (out_4, not_1_out, not_2_out, not_3_out);
  and and_2 (out_5, i0, not_2_out, not_1_out);
  and and_3 (out_6, not_3_out, i1, not_1_out);
  and and_4 (out_7, i0, i1, not_1_out);
  and and_5 (out_8, not_3_out, not_2_out, i2);
  and and_6 (out_9, i0, not_2_out, i2);
  and and_7 (out_10, not_3_out, i1, i2);
  and and_8 (out_11, i0, i1, i2);
endmodule

module _6x3Encoder (
  input  i0,
  input  in_2,
  input  in_3,
  input  in_4,
  input  in_5,
  input  i5,
  output out_7,
  output out_8,
  output out_9
);

  or or_1 (out_7, in_5, i0, in_3);
  or or_2 (out_8, in_2, in_3, i5);
  or or_3 (out_9, i5, in_5, in_4);
endmodule
