// Logisim project ex3lab3.circ as structural Verilog: 2 circuits, main circuit main
module main (
  output out,
  output led
);

  wire and_1_out, and_2_out, and_3_out, clock_1_out, not_1_out, not_2_out, not_3_out, or_1_out, S0, S0_plus,
       S1, S1_plus;

  Button button_1 (.out(S0_plus));
  not not_1 (not_1_out, S0);
  Clock clock_1 (.out(clock_1_out));
  not not_2 (not_2_out, S1);
  D_Flip_Flop d_ff_1 (.clk(clock_1_out), .D(S0_plus), .Q(S0));  // open: Qn, preset, en, reset
  not not_3 (not_3_out, S0_plus);
  and and_1 (and_1_out, S0, S0_plus);
  and and_2 (and_2_out, not_2_out, S0, not_3_out);
  and and_3 (and_3_out, S1, or_1_out);
  or or_1 (or_1_out, not_1_out, and_1_out);
  or or_2 (S1_plus, and_2_out, and_3_out);
  D_Flip_Flop d_ff_2 (.clk(clock_1_out), .D(S1_plus), .Q(S1));  // open: Qn, preset, en, reset
  xor xor_1 (led, S0_plus, S1_plus);

  assign out = led;
endmodule

module d_flipflop (
  input  D,
  input  clock,
  output out_3
);

  wire nand_1_out, nand_2_out, nand_4_out, not_1_out;

  not not_1 (not_1_out, D);
  nand nand_1 (nand_1_out, D, clock);
  nand nand_2 (nand_2_out, clock, not_1_out);
  nand nand_3 (out_3, nand_1_out, nand_4_out);
  nand nand_4 (nand_4_out, out_3, nand_2_out);
endmodule
