// Logisim project ex1.circ as structural Verilog: 4 circuits, main circuit main
module main (
  input  I_O_enable,
  input  A2,
  input  A1,
  input  A0,
  input  A3,
  output WIPERS,
  output ES,
  output D3,
  output D2,
  output D1,
  output D0,
  output AC
);

  wire clock_1_out, n3x8decoder_1_out_4, n3x8decoder_1_out_5, n3x8decoder_1_out_6, n3x8decoder_1_out_7,
       n3x8decoder_1_out_8, n3x8decoder_1_out_9, n3x8decoder_1_out_10, n3x8decoder_1_out_11,
       n8bitenabler_1_out_11, n8bitenabler_1_out_12, n8bitenabler_1_out_13, n8bitenabler_1_out_14,
       n8bitenabler_1_out_15, n8bitenabler_1_out_16, n8bitenabler_1_out_17, n8x8inverter_1_out_10,
       n8x8inverter_1_out_11, n8x8inverter_1_out_12, n8x8inverter_1_out_13, n8x8inverter_1_out_14,
       n8x8inverter_1_out_15, n8x8inverter_1_out_16, n8x8inverter_1_out_17;

  _8x8inverter u_8x8inverter_1 (
    .ON_OFF(A3), .in_2(n3x8decoder_1_out_11), .in_3(n3x8decoder_1_out_10), .in_4(n3x8decoder_1_out_9),
    .in_5(n3x8decoder_1_out_8), .in_6(n3x8decoder_1_out_7), .in_7(n3x8decoder_1_out_6),
    .in_8(n3x8decoder_1_out_5), .in_9(n3x8decoder_1_out_4), .out_10(n8x8inverter_1_out_10),
    .out_11(n8x8inverter_1_out_11), .out_12(n8x8inverter_1_out_12), .out_13(n8x8inverter_1_out_13),
    .out_14(n8x8inverter_1_out_14), .out_15(n8x8inverter_1_out_15), .out_16(n8x8inverter_1_out_16),
    .out_17(n8x8inverter_1_out_17));
  _3x8decoder u_3x8decoder_1 (
    .out_4(n3x8decoder_1_out_4), .out_5(n3x8decoder_1_out_5), .out_6(n3x8decoder_1_out_6),
    .out_7(n3x8decoder_1_out_7), .out_8(n3x8decoder_1_out_8), .out_9(n3x8decoder_1_out_9),
    .out_10(n3x8decoder_1_out_10), .out_11(n3x8decoder_1_out_11), .i2(A2), .i1(A1), .i0(A0));
  _8bitenabler u_8bitenabler_1 (
    .ON_OFF(I_O_enable), .in_2(n8x8inverter_1_out_10), .in_3(n8x8inverter_1_out_11),
    .in_4(n8x8inverter_1_out_12), .in_5(n8x8inverter_1_out_13), .in_6(n8x8inverter_1_out_14),
    .in_7(n8x8inverter_1_out_15), .in_8(n8x8inverter_1_out_16), .in_9(n8x8inverter_1_out_17),
    .out_11(n8bitenabler_1_out_11), .out_12(n8bitenabler_1_out_12), .out_13(n8bitenabler_1_out_13),
    .out_14(n8bitenabler_1_out_14), .out_15(n8bitenabler_1_out_15), .out_16(n8bitenabler_1_out_16),
    .out_17(n8bitenabler_1_out_17));  // open: out_10
  Clock clock_1 (.out(clock_1_out));
  D_Flip_Flop d_ff_1 (.clk(clock_1_out), .D(n8bitenabler_1_out_11), .Q(WIPERS));  // open: Qn, preset, en, reset
  D_Flip_Flop d_ff_2 (.clk(clock_1_out), .D(n8bitenabler_1_out_12), .Q(ES));  // open: Qn, preset, en, reset
  D_Flip_Flop d_ff_3 (.clk(clock_1_out), .D(n8bitenabler_1_out_13), .Q(D3));  // open: Qn, preset, en, reset
  D_Flip_Flop d_ff_4 (.clk(clock_1_out), .D(n8bitenabler_1_out_14), .Q(D2));  // open: Qn, preset, en, reset
  D_Flip_Flop d_ff_5 (.clk(clock_1_out), .D(n8bitenabler_1_out_15), .Q(D1));  // open: Qn, preset, en, reset
  D_Flip_Flop d_ff_6 (.clk(clock_1_out), .D(n8bitenabler_1_out_16), .Q(D0));  // open: Qn, preset, en, reset
  D_Flip_Flop d_ff_7 (.clk(clock_1_out), .D(n8bitenabler_1_out_17), .Q(AC));  // open: Qn, preset, en, reset
endmodule

module _3x8decoder (
  input  i2,
  input  i1,
  input  i0,
  output out_4,
  output out_5,
  output out_6,
  output out_7,
  output out_8,
  output out_9,
  output out_10,
  output out_11
);

  wire not_1_out, not_2_out, not_3_out;

  not not_1 (not_1_out, i2);
  not not_2 (not_2_out, i1);
  not not_3 (not_3_out, i0);
  and and_1 (out_4, not_1_out, not_2_out, not_3_out);
  and and_2 (out_5, i0, not_2_out, not_1_out);
  and and_3 (out_6, not_3_out, i1, not_1_out);
  and and_4 (out_7, i0, i1, not_1_out);
  and and_5 (out_8, not_3_out, not_2_out, i2);
  and and_6 (out_9, i0, not_2_out, i2);
  and and_7 (out_10, not_3_out, i1, i2);
  and and_8 (out_11, i0, i1, i2);
endmodule

module _8x8inverter (
  input  ON_OFF,
  input  in_2,
  input  in_3,
  input  in_4,
  input  in_5,
  input  in_6,
  input  in_7,
  input  in_8,
  input  in_9,
  output out_10,
  output out_11,
  output out_12,
  output out_13,
  output out_14,
  output out_15,
  output out_16,
  output out_17
);

  wire and_1_out, and_2_out, and_3_out, and_4_out, and_5_out, and_6_out, and_7_out, and_8_out, and_9_out,
       and_10_out, and_11_out, and_12_out, and_13_out, and_14_out, and_15_out, and_16_out, not_1_out,
       not_2_out, not_3_out, not_4_out, not_5_out, not_6_out, not_7_out, not_8_out, not_9_out, not_10_out,
       not_11_out, not_12_out, not_13_out, not_14_out, not_15_out, not_16_out;

  not not_1 (not_1_out, in_2);
  not not_2 (not_2_out, in_4);
  not not_3 (not_3_out, in_6);
  not not_4 (not_4_out, in_8);
  not not_5 (not_5_out, ON_OFF);
  and and_1 (and_1_out, not_5_out, in_2);
  and and_2 (and_2_out, not_1_out, ON_OFF);
  not not_6 (not_6_out, ON_OFF);
  and and_3 (and_3_out, not_6_out, in_4);
  and and_4 (and_4_out, not_2_out, ON_OFF);
  not not_7 (not_7_out, ON_OFF);
  and and_5 (and_5_out, not_7_out, in_6);
  and and_6 (and_6_out, not_3_out, ON_OFF);
  not not_8 (not_8_out, ON_OFF);
  and and_7 (and_7_out, not_8_out, in_8);
  and and_8 (and_8_out, not_4_out, ON_OFF);
  or or_1 (out_10, and_1_out, and_2_out);
  or or_2 (out_12, and_3_out, and_4_out);
  or or_3 (out_14, and_5_out, and_6_out);
  or or_4 (out_16, and_7_out, and_8_out);
  not not_9 (not_9_out, ON_OFF);
  not not_10 (not_10_out, in_3);
  not not_11 (not_11_out, ON_OFF);
  not not_12 (not_12_out, in_5);
  not not_13 (not_13_out, ON_OFF);
  not not_14 (not_14_out, in_7);
  not not_15 (not_15_out, ON_OFF);
  not not_16 (not_16_out, in_9);
  and and_9 (and_9_out, not_9_out, in_3);
  and and_10 (and_10_out, not_10_out, ON_OFF);
  and and_11 (and_11_out, not_11_out, in_5);
  and and_12 (and_12_out, not_12_out, ON_OFF);
  and and_13 (and_13_out, not_13_out, in_7);
  and and_14 (and_14_out, not_14_out, ON_OFF);
  and and_15 (and_15_out, not_15_out, in_9);
  and and_16 (and_16_out, not_16_out, ON_OFF);
  or or_5 (out_11, and_9_out, and_10_out);
  or or_6 (out_13, and_11_out, and_12_out);
  or or_7 (out_15, and_13_out, and_14_out);
  or or_8 (out_17, and_15_out, and_16_out);

  // Other names for the same wires on the sheet: onoff = ON_OFF
endmodule

module _8bitenabler (
  input  ON_OFF,
  input  in_2,
  input  in_3,
  input  in_4,
  input  in_5,
  input  in_6,
  input  in_7,
  input  in_8,
  input  in_9,
  output out_10,
  output out_11,
  output out_12,
  output out_13,
  output out_14,
  output out_15,
  output out_16,
  output out_17
);

  and and_1 (out_10, in_2, ON_OFF);
  and and_2 (out_11, in_3, ON_OFF);
  and and_3 (out_12, in_4, ON_OFF);
  and and_4 (out_13, in_5, ON_OFF);
  and and_5 (out_14, in_6, ON_OFF);
  and and_6 (out_15, in_7, ON_OFF);
  and and_7 (out_16, in_8, ON_OFF);
  and and_8 (out_17, in_9, ON_OFF);

  // Other names for the same wires on the sheet: onoff = ON_OFF
endmodule
