// Logisim project FetchPCUpdate (2).circ as structural Verilog
module Instruction_Fetch (
  input  [7:0] in_1,
  output [1:0] out_2,
  output [4:0] out_3,
  output out_4,
  output out_5
);

  ROM rom_1 (.addr(in_1), .data({out_2, out_5, out_3}));  // open: sel
  not not_1 (out_4, out_5);

  // Notes on the sheet:
  //   contents of rom_1 (hex, n*v repeats v):
  //   40 0 0 0 69 0 0 0 e0 4*0 b2 41 0 0 0 6a 0 0 0 f0 4*0 b3 42 0 0 0 6b 0 0 0 f0 4*0 b4 43 0 0 0 6c 0 0
  //   0 f0 4*0 b5 44 0 0 0 6d 0 0 0 f0 4*0 b6 45 0 0 0 6e 0 0 0 f0 4*0 b7 46 0 0 0 6f 0 0 0 f0 4*0 b8 47 0
  //   0 0 70 0 0 0 f0 4*0 b9 48 0 0 0 71 0 0 0 f0 4*0 ba
endmodule

module PC_Update (
  input  [7:0] in_1,
  output [7:0] out_2
);

  Adder adder_1 (.a(8'h1), .b(in_1), .out(out_2));  // open: cin, cout
endmodule
