// Logisim project alu.circ as structural Verilog: 3 circuits, main circuit HoldSum_ALU
module HoldSum_ALU (
  input  [7:0] valA,
  input  [7:0] valB,
  output [7:0] out_3
);

  _8bits_adder u_8bits_adder_1 (.a(valA), .b(valB), .out_3(out_3));  // open: overflow
endmodule

module full_adder (
  input  cin,
  input  a,
  input  b,
  output out,
  output cout
);

  wire and_1_out, and_2_out, xor_1_out;

  xor xor_1 (xor_1_out, a, b);
  xor xor_2 (out, cin, xor_1_out);
  and and_1 (and_1_out, xor_1_out, cin);
  and and_2 (and_2_out, a, b);
  xor xor_3 (cout, and_1_out, and_2_out);
endmodule

module _8bits_adder (
  input  [7:0] a,
  input  [7:0] b,
  output [7:0] out_3,
  output overflow
);

  wire full_adder_1_cout, full_adder_2_cout, full_adder_3_cout, full_adder_4_cout, full_adder_5_cout,
       full_adder_6_cout, full_adder_7_cout, xnor_1_out, xor_1_out;

  full_adder full_adder_1 (.cin(full_adder_2_cout), .a(a[1]), .b(b[1]), .out(out_3[1]), .cout(full_adder_1_cout));
  full_adder full_adder_2 (.cin(1'b0), .a(a[0]), .b(b[0]), .out(out_3[0]), .cout(full_adder_2_cout));
  xnor xnor_1 (xnor_1_out, b[7], a[7]);
  full_adder full_adder_3 (.cin(full_adder_1_cout), .a(a[2]), .b(b[2]), .out(out_3[2]), .cout(full_adder_3_cout));
  xor xor_1 (xor_1_out, b[7], out_3[7]);
  full_adder full_adder_4 (.cin(full_adder_3_cout), .a(a[3]), .b(b[3]), .out(out_3[3]), .cout(full_adder_4_cout));
  full_adder full_adder_5 (.cin(full_adder_4_cout), .a(a[4]), .b(b[4]), .out(out_3[4]), .cout(full_adder_5_cout));
  and and_1 (overflow, xnor_1_out, xor_1_out);
  full_adder full_adder_6 (.cin(full_adder_5_cout), .a(a[5]), .b(b[5]), .out(out_3[5]), .cout(full_adder_6_cout));
  full_adder full_adder_7 (.cin(full_adder_6_cout), .a(a[6]), .b(b[6]), .out(out_3[6]), .cout(full_adder_7_cout));
  full_adder full_adder_8 (.cin(full_adder_7_cout), .a(a[7]), .b(b[7]), .out(out_3[7]));  // open: cout
endmodule
