// Logisim project main.circ as structural Verilog
module main (
  input  [7:0] valB,
  input  [7:0] valA,
  output [7:0] PC
);

  wire clock, fetch_cicuit_1_out_4, fetch_cicuit_1_out_5, fetch_register_2_rax_on_2,
       fetch_register_2_rbx_on_2;
  wire [1:0] fetch_cicuit_1_out_2, fetch_register_2_ifun_2;
  wire [4:0] fetch_cicuit_1_out_3, fetch_register_2_address_2;
  wire [7:0] NEWPC, Register_File_out_5, Register_File_out_6;

  Clock clock_1 (.out(clock));
  Register register_1 (.D(NEWPC), .Q(PC), .clk(clock));  // open: en, clr
  fetch_cicuit fetch_cicuit_1 (
    .in_1(PC), .out_2(fetch_cicuit_1_out_2), .out_3(fetch_cicuit_1_out_3), .out_4(fetch_cicuit_1_out_4),
    .out_5(fetch_cicuit_1_out_5));
  fetch_register fetch_register_1 (
    .ifun(fetch_register_2_ifun_2), .address(fetch_register_2_address_2), .rax_on(fetch_register_2_rax_on_2),
    .rbx_on(fetch_register_2_rbx_on_2), .clock(clock));  // open: ifun_2, address_2, rax_on_2, rbx_on_2
  fetch_register fetch_register_2 (
    .ifun(fetch_cicuit_1_out_2), .address(fetch_cicuit_1_out_3), .rax_on(fetch_cicuit_1_out_4),
    .rbx_on(fetch_cicuit_1_out_5), .clock(clock), .ifun_2(fetch_register_2_ifun_2),
    .address_2(fetch_register_2_address_2), .rax_on_2(fetch_register_2_rax_on_2),
    .rbx_on_2(fetch_register_2_rbx_on_2));
  decode_register decode_register_1 (
    .out_4(valA), .out_5(valB), .rax_val(Register_File_out_5), .rbx_val(Register_File_out_6), .in_1(clock));
  HoldSum_ALU holdsum_alu_1 (.valA(valB), .valB(valA));  // open: out_3
  pc_predict pc_predict_1 (.in_1(PC), .out_2(NEWPC));
  Register_File Register_File (.out_5(Register_File_out_5), .out_6(Register_File_out_6));  // open: eax, ebx, in_3, in_4

  // Notes on the sheet:
  //   EXECUTE
  //   DECODE
  //   FETCH
  //   new_pc
  //   pc
endmodule

module fetch_cicuit (
  input  [7:0] in_1,
  output [1:0] out_2,
  output [4:0] out_3,
  output out_4,
  output out_5
);

  ROM rom_1 (.addr(in_1), .data({out_2, out_5, out_3}));  // open: sel
  not not_1 (out_4, out_5);

  // Notes on the sheet:
  //   contents of rom_1 (hex, n*v repeats v):
  //   40 0 0 0 69 0 0 0 e0 4*0 b2 41 0 0 0 6a 0 0 0 f0 4*0 b3 42 0 0 0 6b 0 0 0 f0 4*0 b4 43 0 0 0 6c 0 0
  //   0 f0 4*0 b5 44 0 0 0 6d 0 0 0 f0 4*0 b6 45 0 0 0 6e 0 0 0 f0 4*0 b7 46 0 0 0 6f 0 0 0 f0 4*0 b8 47 0
  //   0 0 70 0 0 0 f0 4*0 b9 48 0 0 0 71 0 0 0 f0 4*0 ba
endmodule

module fetch_register (
  input  [1:0] ifun,
  input  [4:0] address,
  input  rax_on,
  input  rbx_on,
  input  clock,
  output [1:0] ifun_2,
  output [4:0] address_2,
  output rax_on_2,
  output rbx_on_2
);

  Register #(.width(2)) register_1 (.D(ifun), .Q(ifun_2), .clk(clock));  // open: en, clr
  Register #(.width(5)) register_2 (.D(address), .Q(address_2), .clk(clock));  // open: en, clr
  Register #(.width(1)) register_3 (.D(rax_on), .Q(rax_on_2), .clk(clock));  // open: en, clr
  Register #(.width(1)) register_4 (.D(rbx_on), .Q(rbx_on_2), .clk(clock));  // open: en, clr
endmodule

module pc_predict (
  input  [7:0] in_1,
  output [7:0] out_2
);

  Adder adder_1 (.a(8'h1), .b(in_1), .out(out_2));  // open: cin, cout
endmodule

module Register_File (
  input  eax,
  input  ebx,
  input  [7:0] in_3,
  input  in_4,
  output [7:0] out_5,
  output [7:0] out_6
);

  wire and_1_out, and_2_out;

  Register register_1 (.D(in_3), .Q(out_5), .clk(and_1_out));  // open: en, clr
  and and_1 (and_1_out, eax, in_4);
  Register register_2 (.D(in_3), .Q(out_6), .clk(and_2_out));  // open: en, clr
  and and_2 (and_2_out, ebx, in_4);
endmodule

module decode_register (
  input  in_1,
  input  [7:0] rax_val,
  input  [7:0] rbx_val,
  output [7:0] out_4,
  output [7:0] out_5
);

  Register register_1 (.D(rax_val), .Q(out_4), .clk(in_1));  // open: en, clr
  Register register_2 (.D(rbx_val), .Q(out_5), .clk(in_1));  // open: en, clr
endmodule
